// Logisim project SevenSegDec.circ as structural Verilog: 1 circuit, main circuit SevenSegDec
module SevenSegDec (
  input  A3,
  input  A2,
  input  A1,
  input  A0,
  output S0,
  output S1,
  output S2,
  output S3,
  output S4,
  output S5,
  output S6
);

  wire and_1_out, and_2_out, and_3_out, and_4_out, and_5_out, and_6_out, and_7_out, and_8_out, nor_1_out,
       nor_2_out, nor_3_out, nor_4_out, nor_5_out, nor_6_out, nor_7_out, nor_8_out, not_1_out;

  not not_1 (not_1_out, A3);
  nor nor_1 (nor_1_out, A1, A2, A3);
  nor nor_2 (nor_2_out, A0, A2, A3);
  nor nor_3 (nor_3_out, A2, A3);
  nor nor_4 (nor_4_out, A0, A1, A3);
  nor nor_5 (nor_5_out, A1, A3);
  nor nor_6 (nor_6_out, A0, A3);
  and and_1 (and_1_out, not_1_out, A2, A1, A0);
  and and_2 (and_2_out, A3, nor_7_out);
  nor nor_7 (nor_7_out, A0, A1, A2);
  nor nor_8 (nor_8_out, A3, A2, A1, A0);
  and and_3 (and_3_out, A0, nor_1_out);
  and and_4 (and_4_out, A1, nor_2_out);
  and and_5 (and_5_out, A0, A1, nor_3_out);
  and and_6 (and_6_out, A2, nor_4_out);
  and and_7 (and_7_out, A0, A2, nor_5_out);
  and and_8 (and_8_out, A1, A2, nor_6_out);
  or or_1 (S0, nor_8_out, and_3_out, and_5_out, and_6_out, and_8_out, and_2_out);
  or or_2 (S1, and_3_out, and_4_out, and_5_out, and_6_out, and_8_out, and_1_out, and_2_out);
  or or_3 (S2, nor_8_out, and_3_out, and_4_out, and_5_out, and_7_out, and_1_out, and_2_out);
  or or_4 (S3, nor_8_out, and_4_out, and_5_out, and_6_out, and_7_out, and_8_out, and_1_out, and_2_out);
  or or_5 (S4, nor_8_out, and_3_out, and_4_out, and_5_out, and_1_out);
  or or_6 (S5, nor_8_out, and_3_out, and_4_out, and_5_out, and_1_out);
  or or_7 (S6, and_3_out, and_4_out, and_5_out, and_6_out, and_7_out, and_8_out, and_1_out, and_2_out);
  _7_Segment_Display u_7_segment_display_1 (.g(S0), .f(S1), .a(S2), .b(S3), .e(S4), .d(S5), .c(S6));  // open: dp

  // Notes on the sheet:
  //   Christian Tonnesen, ID: 260847409
endmodule
