// Logisim project SequentialDivider.circ as structural Verilog: 1 circuit, main circuit Divider
module Divider (
  input  [3:0] Dividend,
  input  [3:0] Divisor,
  input  RESET,
  output [3:0] Quotient,
  output [3:0] Remainder,
  output DONE
);

  wire and_1_out, clock_1_out, not_1_out, not_3_out, shift_register_2_p7, subtractor_1_bout;
  wire [7:0] counter_1_q, shift_register_2_p19, shift_register_2_p27, subtractor_1_out;

  Clock clock_1 (.out(clock_1_out));
  not not_1 (not_1_out, DONE);
  and and_1 (and_1_out, clock_1_out, not_1_out);
  // Shift_Register shift_register_1: pin names not known; wires that end beside it: RESET, and_1_out, shift_register_2_p19[7], shift_register_2_p19[6], shift_register_2_p19[5]
  // Shift_Register shift_register_2: pin names not known; wires that end beside it: 1'b0, Dividend[3], Dividend[2], Dividend[1], Dividend[0], RESET, shift_register_2_p7, and_1_out, 1'b0, Divisor[3], Divisor[2], Divisor[1], Divisor[0], 1'b0, shift_register_2_p19[4], shift_register_2_p19[3], shift_register_2_p19[2], shift_register_2_p19[1], shift_register_2_p19[0], shift_register_2_p27[7], shift_register_2_p27[6], shift_register_2_p27[5], shift_register_2_p27[4], shift_register_2_p27[3], shift_register_2_p27[2], shift_register_2_p27[1], shift_register_2_p27[0]
  not not_2 (shift_register_2_p7, RESET);
  Counter #(.max('h5), .ongoal("stay")) counter_1 (
    .clr(RESET), .up(clock_1_out), .count(clock_1_out), .clk(clock_1_out), .Q(counter_1_q));  // open: load, D, carry
  and and_2 (DONE, counter_1_q[0], counter_1_q[2]);
  Subtractor subtractor_1 (
    .a(shift_register_2_p19), .b(shift_register_2_p27), .out(subtractor_1_out), .bout(subtractor_1_bout));  // open: bin
  not not_3 (not_3_out, subtractor_1_bout);
  // Shift_Register #(.length(4)) shift_register_3: pin names not known; wires that end beside it: RESET, and_1_out, not_3_out, subtractor_1_out[2], subtractor_1_out[1], subtractor_1_out[0], Quotient[0], Quotient[1], Quotient[2], Quotient[3], Remainder[2], Remainder[1], Remainder[0]
  // Shift_Register shift_register_4: pin names not known; wires that end beside it: RESET, DONE, DONE, subtractor_1_out[3], Remainder[3]

  // Notes on the sheet:
  //   Christian Tonnesen, ID: 260847409
endmodule
