// Logisim project SequentialMultipler.circ as structural Verilog: 1 circuit, main circuit Multiplier
module Multiplier (
  input  [3:0] A,
  input  [3:0] B,
  input  RESET,
  output [7:0] PRODUCT,
  output DONE
);

  wire and_1_out, clock_1_out, counter_1_carry, not_1_out, shift_register_1_p2, shift_register_2_p6,
       shift_register_2_p19;
  wire [7:0] adder_1_out, counter_1_q, multiplexer_1_out, shift_register_1_p7;

  Clock clock_1 (.out(clock_1_out));
  not not_1 (not_1_out, counter_1_carry);
  and and_1 (and_1_out, clock_1_out, not_1_out);
  Counter #(.max('h9), .ongoal("load")) counter_1 (
    .clr(RESET), .up(clock_1_out), .count(clock_1_out), .clk(clock_1_out), .carry(counter_1_carry),
    .Q(counter_1_q));  // open: load, D
  // Shift_Register shift_register_1: pin names not known; wires that end beside it: RESET, shift_register_1_p2, and_1_out, 1'b0, A[0], A[1], shift_register_1_p7[0], shift_register_1_p7[1]
  not not_2 (shift_register_1_p2, RESET);
  // Shift_Register #(.length(4)) shift_register_2: pin names not known; wires that end beside it: A[2], A[3], 1'b0, 1'b0, RESET, shift_register_2_p6, and_1_out, 1'b0, B[3], B[2], B[1], B[0], shift_register_1_p7[2], shift_register_1_p7[3], shift_register_1_p7[4], shift_register_1_p7[5], shift_register_1_p7[6], shift_register_1_p7[7], shift_register_2_p19
  not not_3 (shift_register_2_p6, RESET);
  Multiplexer #(.enable("false"), .width(8)) multiplexer_1 (
    .in0({8{1'b0}}), .in1(shift_register_1_p7), .out(multiplexer_1_out), .sel(shift_register_2_p19));
  and and_2 (DONE, counter_1_q[0], counter_1_q[3]);
  Register register_1 (.D(adder_1_out), .clk(and_1_out), .Q(PRODUCT), .clr(RESET));  // open: en
  Adder adder_1 (.a(multiplexer_1_out), .b(PRODUCT), .out(adder_1_out));  // open: cin, cout

  // Notes on the sheet:
  //   Christian Tonnesen, ID: 260847409
endmodule
