// Logisim project led.circ as structural Verilog: 1 circuit, main circuit main
module main (
);

  wire clock_1_out, decoder_1_out0, decoder_1_out1, decoder_1_out2, decoder_1_out3, decoder_1_out4,
       decoder_1_out5, decoder_1_out6, decoder_1_out7, decoder_1_out8, or_1_out, or_2_out;
  wire [3:0] counter_1_q;

  Counter #(.max('h8), .width(4)) counter_1 (
    .clk(clock_1_out), .Q(counter_1_q));  // open: clr, load, up, count, D, carry
  Clock clock_1 (.out(clock_1_out));
  LED led_1 (.in(or_1_out));
  or or_1 (or_1_out, decoder_1_out7, decoder_1_out2);
  LED led_2 ();  // open: in
  LED led_3 (.in(decoder_1_out0));
  Decoder #(.select(4)) decoder_1 (
    .out0(decoder_1_out0), .out1(decoder_1_out1), .out2(decoder_1_out2), .out3(decoder_1_out3),
    .out4(decoder_1_out4), .out5(decoder_1_out5), .out6(decoder_1_out6), .out7(decoder_1_out7),
    .out8(decoder_1_out8), .sel(counter_1_q));  // open: out9, out10, out11, out12, out13, out14, out15, en
  LED led_4 (.in(or_2_out));
  LED led_5 ();  // open: in
  or or_2 (or_2_out, decoder_1_out4, decoder_1_out6);
  LED led_6 ();  // open: in
  LED led_7 (.in(decoder_1_out1));
  LED led_8 (.in(decoder_1_out5));
  LED led_9 (.in(decoder_1_out3));
  LED led_10 (.in(decoder_1_out8));

  // Notes on the sheet:
  //   1
  //   0
  //   2
  //   3
  //   Christian Tonnesen, ID: 260847409
  //   5
  //   4
  //   6
  //   7
  //   8
  //   9
endmodule
